# Fritzing sketch Piano_10_Touches (saved by Fritzing 0.9.2b)
breadboards: 1

parts:
  Composant1 = Arduino Uno (Rev3)
  J1 = Piezo Speaker
  J2 = Piezo Speaker
  R2 = Resistor [tolerance=±5% resistance=1M package=THT]
  R3 = Resistor [tolerance=±5% resistance=1M package=THT]
  R4 = Resistor [tolerance=±5% resistance=1M package=THT]
  R5 = Resistor [tolerance=±5% resistance=1M package=THT]
  R6 = Resistor [tolerance=±5% resistance=1M package=THT]
  ANT1 = Antenna
  ANT2 = Antenna
  ANT3 = Antenna
  ANT4 = Antenna
  ANT5 = Antenna
  R8 = Resistor [tolerance=±5% resistance=330 package=THT]
  R9 = Resistor [tolerance=±5% resistance=1M package=THT]
  R10 = Resistor [tolerance=±5% resistance=1M package=THT]
  R11 = Resistor [tolerance=±5% resistance=1M package=THT]
  R12 = Resistor [tolerance=±5% resistance=1M package=THT]
  R13 = Resistor [tolerance=±5% resistance=1M package=THT]
  ANT6 = Antenna
  ANT7 = Antenna
  ANT8 = Antenna
  ANT9 = Antenna
  ANT10 = Antenna
  R14 = Resistor [tolerance=±5% resistance=330 package=THT]

nets:
  N1: Composant1.D8, R13.Pin_0, ANT6.antenna_lead
  N2: Composant1.D9_PWM, R12.Pin_0, ANT7.antenna_lead
  N3: Composant1.D10_PWM/SS, R11.Pin_0, ANT8.antenna_lead
  N4: Composant1.D11_PWM/MOSI, R10.Pin_0, ANT9.antenna_lead
  N5: Composant1.D12/MISO, R9.Pin_0, ANT10.antenna_lead
  N6: Composant1.D13/SCK, R8.Pin_0, R14.Pin_0
  N7: Composant1.GND, J1.pin1, J2.pin1
  N8: Composant1.D2, R2.Pin_0, R3.Pin_0, R4.Pin_0, R5.Pin_0, R6.Pin_0, R9.Pin_1, R10.Pin_1, R11.Pin_1, R12.Pin_1, R13.Pin_1
  N9: Composant1.D3_PWM, R2.Pin_1, ANT4.antenna_lead
  N10: Composant1.D4, R3.Pin_1, ANT5.antenna_lead
  N11: Composant1.D5_PWM, R4.Pin_1, ANT1.antenna_lead
  N12: Composant1.D6_PWM, R5.Pin_1, ANT2.antenna_lead
  N13: Composant1.D7, R6.Pin_1, ANT3.antenna_lead
  N14: J1.pin2, R8.Pin_1
  N15: J2.pin2, R14.Pin_1

notes:
  1 000 000 ohms
  220 ohms
