# Fritzing sketch MyMagicStick_BT (saved by Fritzing 0.9.2b)
circuit board: 8.46667cm x 5.64444cm
breadboards: 1

parts:
  Alimentation_Externe = Battery block 9V
  Composant1 = Arduino Uno (Rev3)
  Composant2 = FC-28 Soil Hygrometer Module
  Composant3 = FC-28 Soil Hygrometer Module - Probe
  DHT1 = DHT11 Humitidy and Temperature Sensor
  Luminosité = Grove Light Sensor
  Composant4 = Module Bluetooth

nets:
  N1: Alimentation_Externe.+, Composant1.VIN
  N2: Composant1.A0, Composant2.AO
  N3: Composant1.A1, Luminosité.SIG
  N4: Composant1.D0/RX, Composant4.RXD
  N5: Composant1.D1/TX, Composant4.TXD
  GND: Composant1.GND, Composant2.GND, DHT1.GND, Luminosité.GND, Composant4.GND
  VCC: Composant2.VCC, DHT1.VDD, Luminosité.VCC, Composant4.VCC
  N6: Composant2.POS, Composant3.POS
  N7: Composant2.NEG, Composant3.NEG

custom parts:
  FC-28 Soil Hygrometer Module: The FC-28 is a soil hygrometer module that uses the Texas Instruments LM393 comparator chip to provide an analog measurement of soil humidity. The digital output is high when soil moisture is over a certain threshold, as determined by adjusting the potentiometer.
  FC-28 Soil Hygrometer Module - Probe: The FC-28 is a soil hygrometer module that uses the Texas Instruments LM393 comparator chip to provide an analog measurement of soil humidity.
  DHT11 Humitidy and Temperature Sensor: DHT11 Humidity and Temperature Sensor
