# Fritzing sketch MyMagicStick_Wifi (saved by Fritzing 0.9.2b)
circuit board: 8.46667cm x 5.64444cm
breadboards: 1

parts:
  D1 = Rectifier Diode [part_number=1N4001 package="300 mil [THT]"]
  R1 = Resistor [tolerance=±5% resistance=220 package=THT]
  Alimentation_Externe = Battery block 9V
  Composant1 = Arduino Uno (Rev3)
  Composant2 = FC-28 Soil Hygrometer Module
  Composant3 = FC-28 Soil Hygrometer Module - Probe
  DHT1 = DHT11 Humitidy and Temperature Sensor
  Luminosité = Grove Light Sensor
  U2 = ESP8266 WiFi Module [part_number=ESP8266]
  IC1 = IC, DIP package, 16 pins [chip_label=IC]

nets:
  N1: D1.cathode, R1.Pin_0, U2.VCC, U2.GPIO_0, U2.GPIO_2, U2.CH_PD, U2.GPIO_15, U2.GPIO_4, U2.GPIO_5, U2.ADC_0, U2.GPIO_16, U2.GPIO_14, U2.GPIO_12, U2.GPIO_13, U2.REST, IC1.pin1
  N2: D1.anode, Alimentation_Externe.+, Composant1.VIN
  GND: R1.Pin_1, Alimentation_Externe.-, Composant1.GND, Composant2.GND, DHT1.GND, Luminosité.GND, U2.GND, IC1.pin8
  N3: Composant1.A0, DHT1.DATA
  N4: Composant1.A1, Luminosité.SIG
  N5: Composant1.D0/RX, U2.TXD
  N6: Composant1.D1/TX, IC1.pin3
  VCC: Composant1.5V, Composant2.VCC, DHT1.VDD, Luminosité.VCC
  N7: Composant2.POS, Composant3.POS
  N8: Composant2.NEG, Composant3.NEG
  N9: U2.RXD, IC1.pin2

notes:
  DC4050
  D0

custom parts:
  FC-28 Soil Hygrometer Module: The FC-28 is a soil hygrometer module that uses the Texas Instruments LM393 comparator chip to provide an analog measurement of soil humidity. The digital output is high when soil moisture is over a certain threshold, as determined by adjusting the potentiometer.
  FC-28 Soil Hygrometer Module - Probe: The FC-28 is a soil hygrometer module that uses the Texas Instruments LM393 comparator chip to provide an analog measurement of soil humidity.
  DHT11 Humitidy and Temperature Sensor: DHT11 Humidity and Temperature Sensor
